# Fritzing sketch ESP82_CO2 (saved by Fritzing 0.9.3b)
circuit board: 6.30344cm x 7.60344cm
breadboards: 1

parts:
  ESP8266 = NodeMCU V3.0
  Boton = Pushbutton [package=THT]
  Pantalla = TM1637
  R1 = Resistor [tolerance=±5% resistance=10k package=THT]
  Buzzer = KY-012 Active Buzzer Module [package="Breakout board"]
  R2 = Resistor [tolerance=±5% resistance=220 package=THT]
  R3 = Resistor [tolerance=±5% resistance=220 package=THT]
  R4 = Resistor [tolerance=±5% resistance=220 package=THT]
  Scd30/0220 = SCD30
  LED = RGB LED - (4 legs) [package="5 mm [THT]"]
  USB = Header 6 [package=molex-1x6-ra]
  s8lp = Header 6 [package=molex-1x6-ra]
  s8lp1 = Header 6 [package=molex-1x6-ra]

nets:
  N1: ESP8266.D0, R3.Pin_1
  N2: ESP8266.D1, Scd30/0220.TX/SCL, s8lp.4
  N3: ESP8266.D2, Scd30/0220.RX/SDA, s8lp.5
  N4: ESP8266.D3, Boton.leg0, R1.Pin_0
  N5: ESP8266.D4, Buzzer.S
  N6: ESP8266.3V3, R1.Pin_1
  N7: ESP8266.GND#6, ESP8266.GND#13, ESP8266.GND#16, ESP8266.GND#33, Boton.leg1, Pantalla.GND, Buzzer.-, USB.5
  N8: ESP8266.D5, Pantalla.CLK
  N9: ESP8266.D6, Pantalla.DIO
  N10: ESP8266.D7, R4.Pin_1
  N11: ESP8266.D8, R2.Pin_1
  N12: ESP8266.Vin, USB.1
  VCC: ESP8266.VU, Pantalla.VCC, Buzzer.VCC, Scd30/0220.VDD, LED.common_anode, s8lp1.6
  N13: ESP8266.GND#41, Scd30/0220.GND, s8lp1.5
  N14: R2.Pin_0, LED.blue_cathode
  N15: R3.Pin_0, LED.red_cathode
  N16: R4.Pin_0, LED.green_cathode

notes:
  SCD30
  PANTALLA
  BUZZER
  LED
  BOTON

custom parts:
  NodeMCU V3.0: ESP8266 based NodeMCU
  TM1637: A 4 7-seg display
  KY-012 Active Buzzer Module: Active Piezoelectric Buzzer Module KY-012, it produces single-tone sound when signal is high. (Special thanks to vanepp for fixing the PCB holes and other errors)
  SCD30: CO2 , humidity, and temperature sensor * Current consumption: 19 mA @ 1 meas. per 2 s. * Digital interface UART or I2C * Company: Sensirion - The Sensor Company Electrical specifications * average current: 19 mA * max. current: 75 mA * DC supply: 3.3 V - 5.5 V Operation conditions * temperature: 0 – 50°C * humidity: 0 – 95 %RH * sensor lifetime: 15 years CO2-sensor: * NDIR CO 2 sensor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
