# Fritzing sketch ESP82_CO2 (saved by Fritzing 0.9.3b)
circuit board: 6.30344cm x 7.60344cm
breadboards: 1

parts:
  Boton = Pushbutton [package=THT]
  R1 = Resistor [tolerance=±5% resistance=10k package=THT]
  R2 = Resistor [tolerance=±5% resistance=220 package=THT]  # not connected
  R3 = Resistor [tolerance=±5% resistance=220 package=THT]  # not connected
  R4 = Resistor [tolerance=±5% resistance=220 package=THT]  # not connected

nets:
  N1: Boton.leg0, R1.Pin_0

notes:
  SCD30
  PANTALLA
  BUZZER
  LED
  BOTON
  usb
  scd30/0220
  pantalla
  led
  s8lp
  Buzzer
