# Fritzing sketch UniversalShield (saved by Fritzing 0.9.6b)
circuit board: 6.88566cm x 5.36311cm
breadboards: 1

parts:
  Arduino_WiFi_Rev_2 = Arduino Uno (Rev3)
  SEN0220 = male pin header, 4 pins [form="♂ (male)"]
  DISPLAY = male pin header, 4 pins [form="♂ (male)"]
  T3022 = male pin header, 4 pins [form="♂ (male)"]

nets:
  N1: Arduino_WiFi_Rev_2.A4/SDA, T3022.pin3
  N2: Arduino_WiFi_Rev_2.A5/SCL, T3022.pin4
  GND: Arduino_WiFi_Rev_2.GND, SEN0220.pin3, DISPLAY.pin4, T3022.pin2
  N3: Arduino_WiFi_Rev_2.D0/RX, SEN0220.pin1
  N4: Arduino_WiFi_Rev_2.D1/TX, SEN0220.pin2
  N5: Arduino_WiFi_Rev_2.D6_PWM, DISPLAY.pin1
  N6: Arduino_WiFi_Rev_2.D7, DISPLAY.pin2
  5V: Arduino_WiFi_Rev_2.5V, SEN0220.pin4, DISPLAY.pin3, T3022.pin1
